# Fritzing sketch Safe Distance Project Fritzing (saved by Fritzing 0.8.7b)
breadboards: 1

parts:
  Part1 = Arduino Uno (Rev3)
  J1 = Piezo Speaker
  U1 = LCD-16X2 [package=lcd-16x2]  # not connected
  R1 = Resistor [tolerance=±5% resistance=220 package=THT]
  LED1 = LED - 5mm [color="Red (633nm)" package="5 mm [THT]"]
  LED2 = LED - 5mm [color="Green (565nm)" package="5 mm [THT]"]
  R2 = Resistor [tolerance=±5% resistance=220 package=THT]
  R3 = Resistor [tolerance=±5% resistance=220 package=THT]
  J2 = Infrared Proximity Sensor

nets:
  N1: Part1.D9_PWM, LED2.anode
  N2: Part1.D10_PWM/SS, LED1.anode
  N3: Part1.D13/SCK, J1.pin2
  N4: Part1.D7, J2.Vout
  5V: Part1.5V, R1.Pin_1, J2.Vcc
  GND: Part1.GND, J1.pin1, R2.Pin_0, R3.Pin_0, J2.GND
  N5: LED1.cathode, R2.Pin_1
  N6: LED2.cathode, R3.Pin_1

notes:
  This is a ultra sonic sensor replacement and pin 7is suppose to go Trig, and ping 6 goes to Echo.
